// Logisim project logismDesign.circ as structural Verilog
// RegisterFile
module Register_File (
  input  [17:0] inputData,
  input  [3:0] ReadReg1Address,
  input  [3:0] ReadReg2Address,
  input  [3:0] destReg,
  input  registerWrite,
  input  Clock,
  input  Clear,
  output [17:0] Reg1DataBinary,
  output [17:0] Reg2DataBinary
);

  wire _0_out, _8_out, _15_out, and_1_out, and_2_out, and_3_out, and_4_out, and_5_out, and_6_out, and_7_out,
       and_8_out, and_9_out, and_10_out, and_11_out, and_12_out, and_13_out, decoder_1_out0, decoder_1_out1,
       decoder_1_out2, decoder_1_out3, decoder_1_out4, decoder_1_out5, decoder_1_out6, decoder_1_out7,
       decoder_1_out8, decoder_1_out9, decoder_1_out10, decoder_1_out11, decoder_1_out12, decoder_1_out13,
       decoder_1_out14, decoder_1_out15;
  wire [17:0] R0_q, R1_q, R2_q, R3_q, R4_q, R5_q, R6_q, R7_q, R8_q, R9_q, R10_q, R11_q, R12_q, R13_q, R14_q,
       R15_q;

  Decoder #(.select(4)) decoder_1 (
    .out0(decoder_1_out0), .out1(decoder_1_out1), .out2(decoder_1_out2), .out3(decoder_1_out3),
    .out4(decoder_1_out4), .out5(decoder_1_out5), .out6(decoder_1_out6), .out7(decoder_1_out7),
    .out8(decoder_1_out8), .out9(decoder_1_out9), .out10(decoder_1_out10), .out11(decoder_1_out11),
    .out12(decoder_1_out12), .out13(decoder_1_out13), .out14(decoder_1_out14), .out15(decoder_1_out15),
    .sel(destReg));  // open: en
  // Probe on inputData
  and _0 (_0_out, decoder_1_out0, registerWrite);
  and and_1 (and_1_out, decoder_1_out1, registerWrite);
  and and_2 (and_2_out, decoder_1_out2, registerWrite);
  and and_3 (and_3_out, decoder_1_out3, registerWrite);
  and and_4 (and_4_out, decoder_1_out4, registerWrite);
  and and_5 (and_5_out, decoder_1_out5, registerWrite);
  and and_6 (and_6_out, decoder_1_out6, registerWrite);
  and _8 (_8_out, decoder_1_out7, registerWrite);
  and and_7 (and_7_out, decoder_1_out8, registerWrite);
  and and_8 (and_8_out, decoder_1_out9, registerWrite);
  and and_9 (and_9_out, decoder_1_out10, registerWrite);
  and and_10 (and_10_out, decoder_1_out11, registerWrite);
  and and_11 (and_11_out, decoder_1_out12, registerWrite);
  and and_12 (and_12_out, decoder_1_out13, registerWrite);
  and and_13 (and_13_out, decoder_1_out14, registerWrite);
  and _15 (_15_out, decoder_1_out15, registerWrite);
  Register #(.width(18)) R0 (.D(inputData), .en(_0_out), .Q(R0_q), .clk(Clock), .clr(Clear));
  Register #(.width(18)) R1 (.D(inputData), .en(and_1_out), .Q(R1_q), .clk(Clock), .clr(Clear));
  Register #(.width(18)) R2 (.D(inputData), .en(and_2_out), .Q(R2_q), .clk(Clock), .clr(Clear));
  Register #(.width(18)) R3 (.D(inputData), .en(and_3_out), .Q(R3_q), .clk(Clock), .clr(Clear));
  Register #(.width(18)) R4 (.D(inputData), .en(and_4_out), .Q(R4_q), .clk(Clock), .clr(Clear));
  Register #(.width(18)) R5 (.D(inputData), .en(and_5_out), .Q(R5_q), .clk(Clock), .clr(Clear));
  Register #(.width(18)) R6 (.D(inputData), .en(and_6_out), .Q(R6_q), .clk(Clock), .clr(Clear));
  Register #(.width(18)) R7 (.D(inputData), .en(_8_out), .Q(R7_q), .clk(Clock), .clr(Clear));
  Register #(.width(18)) R8 (.en(and_7_out), .Q(R8_q), .clk(Clock), .clr(Clear));  // open: D
  Register #(.width(18)) R9 (.D(inputData), .en(and_8_out), .Q(R9_q), .clk(Clock), .clr(Clear));
  Register #(.width(18)) R10 (.D(inputData), .en(and_9_out), .Q(R10_q), .clk(Clock), .clr(Clear));
  Register #(.width(18)) R11 (.D(inputData), .en(and_10_out), .Q(R11_q), .clk(Clock), .clr(Clear));
  Register #(.width(18)) R12 (.D(inputData), .en(and_11_out), .Q(R12_q), .clk(Clock), .clr(Clear));
  Register #(.width(18)) R13 (.D(inputData), .en(and_12_out), .Q(R13_q), .clk(Clock), .clr(Clear));
  Register #(.width(18)) R14 (.D(inputData), .en(and_13_out), .Q(R14_q), .clk(Clock), .clr(Clear));
  Register #(.width(18)) R15 (.D(inputData), .en(_15_out), .Q(R15_q), .clk(Clock), .clr(Clear));
  Multiplexer #(.select(4), .width(18)) multiplexer_1 (
    .in0(R0_q), .in1(R1_q), .in2(R2_q), .in3(R3_q), .in4(R4_q), .in5(R5_q), .in6(R6_q), .in7(R7_q),
    .in8(R8_q), .in9(R9_q), .in10(R10_q), .in11(R11_q), .in12(R12_q), .in13(R13_q), .in14(R14_q),
    .in15(R15_q), .out(Reg1DataBinary), .sel(ReadReg1Address));  // open: en
  Multiplexer #(.select(4), .width(18)) multiplexer_2 (
    .in0(R0_q), .in1(R1_q), .in2(R2_q), .in3(R3_q), .in4(R4_q), .in5(R5_q), .in6(R6_q), .in7(R7_q),
    .in8(R8_q), .in9(R9_q), .in10(R10_q), .in11(R11_q), .in12(R12_q), .in13(R13_q), .in14(R14_q),
    .in15(R15_q), .out(Reg2DataBinary), .sel(ReadReg2Address));  // open: en
endmodule

module Half_Adder (
  input  a,
  input  b,
  output sum,
  output count
);

  xor xor_1 (sum, a, b);
  and and_1 (count, a, b);
endmodule

module Full_Adder (
  input  a,
  input  b,
  input  C_in,
  output sum,
  output C_out
);

  wire and_1_out, and_2_out, or_2_out;

  xor xor_1 (sum, a, b, C_in);
  and and_1 (and_1_out, a, ~C_in, b);  // AND_Gate
  or or_1 (C_out, and_1_out, and_2_out);
  or or_2 (or_2_out, b, a);
  and and_2 (and_2_out, C_in, or_2_out);
endmodule

module Adder (
  input  [17:0] \ınputA ,
  input  [17:0] InputB,
  output [17:0] Output
);

  wire full_adder_1_c_out, full_adder_2_c_out, full_adder_3_c_out, full_adder_4_c_out, full_adder_5_c_out,
       full_adder_6_c_out, full_adder_7_c_out, full_adder_8_c_out, full_adder_9_c_out, full_adder_10_c_out,
       full_adder_11_c_out, full_adder_12_c_out, full_adder_13_c_out, full_adder_14_c_out,
       full_adder_15_c_out, full_adder_16_c_out, half_adder_1_count;

  Half_Adder half_adder_1 (.a(\ınputA [0]), .b(InputB[0]), .sum(Output[0]), .count(half_adder_1_count));
  Full_Adder full_adder_1 (
    .a(\ınputA [1]), .b(half_adder_1_count), .C_in(InputB[1]), .sum(Output[1]), .C_out(full_adder_1_c_out));
  Full_Adder full_adder_2 (
    .a(\ınputA [2]), .b(full_adder_1_c_out), .C_in(InputB[2]), .sum(Output[2]), .C_out(full_adder_2_c_out));
  Full_Adder full_adder_3 (
    .a(\ınputA [3]), .b(full_adder_2_c_out), .C_in(InputB[3]), .sum(Output[3]), .C_out(full_adder_3_c_out));
  Full_Adder full_adder_4 (
    .a(\ınputA [4]), .b(full_adder_3_c_out), .C_in(InputB[4]), .sum(Output[4]), .C_out(full_adder_4_c_out));
  Full_Adder full_adder_5 (
    .a(\ınputA [5]), .b(full_adder_4_c_out), .C_in(InputB[5]), .sum(Output[5]), .C_out(full_adder_5_c_out));
  Full_Adder full_adder_6 (
    .a(\ınputA [6]), .b(full_adder_5_c_out), .C_in(InputB[6]), .sum(Output[6]), .C_out(full_adder_6_c_out));
  Full_Adder full_adder_7 (
    .a(\ınputA [7]), .b(full_adder_6_c_out), .C_in(InputB[7]), .sum(Output[7]), .C_out(full_adder_7_c_out));
  Full_Adder full_adder_8 (
    .a(\ınputA [8]), .b(full_adder_7_c_out), .C_in(InputB[8]), .sum(Output[8]), .C_out(full_adder_8_c_out));
  Full_Adder full_adder_9 (
    .a(\ınputA [9]), .b(full_adder_8_c_out), .C_in(InputB[9]), .sum(Output[9]), .C_out(full_adder_9_c_out));
  Full_Adder full_adder_10 (
    .a(\ınputA [10]), .b(full_adder_9_c_out), .C_in(InputB[10]), .sum(Output[10]), .C_out(full_adder_10_c_out));
  Full_Adder full_adder_11 (
    .a(\ınputA [11]), .b(full_adder_10_c_out), .C_in(InputB[11]), .sum(Output[11]),
    .C_out(full_adder_11_c_out));
  Full_Adder full_adder_12 (
    .a(\ınputA [12]), .b(full_adder_11_c_out), .C_in(InputB[12]), .sum(Output[12]),
    .C_out(full_adder_12_c_out));
  Full_Adder full_adder_13 (
    .a(\ınputA [13]), .b(full_adder_12_c_out), .C_in(InputB[13]), .sum(Output[13]),
    .C_out(full_adder_13_c_out));
  Full_Adder full_adder_14 (
    .a(\ınputA [14]), .b(full_adder_13_c_out), .C_in(InputB[14]), .sum(Output[14]),
    .C_out(full_adder_14_c_out));
  Full_Adder full_adder_15 (
    .a(\ınputA [15]), .b(full_adder_14_c_out), .C_in(InputB[15]), .sum(Output[15]),
    .C_out(full_adder_15_c_out));
  Full_Adder full_adder_16 (
    .a(\ınputA [16]), .b(full_adder_15_c_out), .C_in(InputB[16]), .sum(Output[16]),
    .C_out(full_adder_16_c_out));
  Full_Adder full_adder_17 (
    .a(\ınputA [17]), .b(full_adder_16_c_out), .C_in(InputB[17]), .sum(Output[17]));  // open: C_out
  // Probe on Output
endmodule

module ALU (
  input  [17:0] src1,
  input  [17:0] src2,
  input  [1:0] ALUcontrol,
  output [17:0] ALUresult
);

  wire decoder_1_out0, decoder_1_out1, decoder_1_out2, decoder_1_out3;
  wire [17:0] adder_1_output, and_1_out, or_1_out, xor_1_out;

  Decoder #(.select(2), .enable("false")) decoder_1 (
    .out0(decoder_1_out0), .out1(decoder_1_out1), .out2(decoder_1_out2), .out3(decoder_1_out3),
    .sel(ALUcontrol));
  assign xor_1_out = src1 ^ src2;  // XOR_Gate xor_1, 18 bits wide
  assign ALUresult = decoder_1_out3 ? xor_1_out : 18'bz;  // Controlled_Buffer controlled_buffer_1
  assign or_1_out = src1 | src2;  // OR_Gate or_1, 18 bits wide
  assign ALUresult = decoder_1_out2 ? or_1_out : 18'bz;  // Controlled_Buffer controlled_buffer_2
  assign and_1_out = src1 & src2;  // AND_Gate and_1, 18 bits wide
  assign ALUresult = decoder_1_out1 ? and_1_out : 18'bz;  // Controlled_Buffer controlled_buffer_3
  // Probe on ALUresult
  Adder adder_1 (.\ınputA (src1), .InputB(src2), .Output(adder_1_output));
  assign ALUresult = decoder_1_out0 ? adder_1_output : 18'bz;  // Controlled_Buffer controlled_buffer_4

  // Notes on the sheet:
  //   3
  //   2
  //   1
  //   ADDR
  //   0
endmodule

// PC Controller
module PC (
  input  [17:0] Addr,
  input  [2:0] nzp,
  input  [2:0] cmp,
  input  isJump,
  input  enable,
  input  clock,
  input  clear,
  output [17:0] PC_Address
);

  wire or_2_out;
  wire [2:0] isB, or_1_out;
  wire [17:0] adder_1_output, demultiplexer_1_out0, demultiplexer_1_out1, multiplexer_1_out, or_3_out;

  assign isB = nzp & cmp;  // AND_Gate and_1, 3 bits wide
  assign or_1_out = isB | {2'b00, isJump};  // OR_Gate or_1, 3 bits wide
  Demultiplexer #(.width(18), .enable("false")) demultiplexer_1 (
    .out0(demultiplexer_1_out0), .out1(demultiplexer_1_out1), .in(multiplexer_1_out), .sel(or_2_out));
  Multiplexer #(.select(3), .width(18), .enable("false")) multiplexer_1 (
    .in0(18'h1), .in1(Addr), .in2(Addr), .in3(Addr), .in4(Addr), .in5(Addr), .in6(Addr), .in7(Addr),
    .out(multiplexer_1_out), .sel(or_1_out));
  or or_2 (or_2_out, isB[2], isB[1], isB[0]);
  assign or_3_out = demultiplexer_1_out1 | adder_1_output;  // OR_Gate or_3, 18 bits wide
  Adder adder_1 (.\ınputA (demultiplexer_1_out0), .InputB(PC_Address), .Output(adder_1_output));
  Register #(.width(18)) PC_Register (.D(or_3_out), .en(enable), .Q(PC_Address), .clk(clock), .clr(clear));

  // Notes on the sheet:
  //   Incrementer
endmodule

// Comparator
module _1_bit_comparator (
  input  input1,
  input  input2,
  input  lt_input,
  input  eq_input,
  input  gt_input,
  output out_6,
  output out_7,
  output out_8
);

  wire and_2_out, and_3_out, not_1_out, not_2_out, xnor_1_out;

  xnor xnor_1 (xnor_1_out, input1, input2);
  and and_1 (out_6, xnor_1_out, lt_input);
  not not_1 (not_1_out, input2);
  and and_2 (and_2_out, input1, not_1_out, lt_input);
  or or_1 (out_7, and_2_out, eq_input);
  not not_2 (not_2_out, input1);
  and and_3 (and_3_out, not_2_out, input2, lt_input);
  or or_2 (out_8, and_3_out, gt_input);
endmodule

// Comparator
module _3_bit_comparator (
  input  [2:0] input1,
  input  lt_input,
  input  eq_input,
  input  gt_input,
  input  [2:0] input2,
  output out_6,
  output out_7,
  output out_8
);

  wire n1_bit_comparator_1_out_6, n1_bit_comparator_1_out_7, n1_bit_comparator_1_out_8,
       n1_bit_comparator_2_out_6, n1_bit_comparator_2_out_7, n1_bit_comparator_2_out_8;

  _1_bit_comparator u_1_bit_comparator_1 (
    .input1(input2[2]), .input2(gt_input), .lt_input(eq_input), .eq_input(lt_input), .gt_input(input1[2]),
    .out_6(n1_bit_comparator_1_out_6), .out_7(n1_bit_comparator_1_out_7), .out_8(n1_bit_comparator_1_out_8));
  _1_bit_comparator u_1_bit_comparator_2 (
    .input1(input2[1]), .input2(n1_bit_comparator_1_out_6), .lt_input(n1_bit_comparator_1_out_7),
    .eq_input(n1_bit_comparator_1_out_8), .gt_input(input1[1]), .out_6(n1_bit_comparator_2_out_6),
    .out_7(n1_bit_comparator_2_out_7), .out_8(n1_bit_comparator_2_out_8));
  _1_bit_comparator u_1_bit_comparator_3 (
    .input1(input2[0]), .input2(n1_bit_comparator_2_out_6), .lt_input(n1_bit_comparator_2_out_7),
    .eq_input(n1_bit_comparator_2_out_8), .gt_input(input1[0]), .out_6(out_8), .out_7(out_7), .out_8(out_6));
endmodule

module Comparator (
  input  [17:0] input1,
  input  lt_input,
  input  eq_input,
  input  gt_input,
  input  [17:0] input2,
  output [2:0] \output 
);

  wire n3_bit_comparator_1_out_6, n3_bit_comparator_1_out_7, n3_bit_comparator_1_out_8,
       n3_bit_comparator_2_out_6, n3_bit_comparator_2_out_7, n3_bit_comparator_2_out_8,
       n3_bit_comparator_3_out_6, n3_bit_comparator_3_out_7, n3_bit_comparator_3_out_8,
       n3_bit_comparator_4_out_6, n3_bit_comparator_4_out_7, n3_bit_comparator_4_out_8,
       n3_bit_comparator_5_out_6, n3_bit_comparator_5_out_7, n3_bit_comparator_5_out_8;

  _3_bit_comparator u_3_bit_comparator_1 (
    .input1(input1[17:15]), .lt_input(lt_input), .eq_input(eq_input), .gt_input(gt_input),
    .input2(input2[17:15]), .out_6(n3_bit_comparator_1_out_6), .out_7(n3_bit_comparator_1_out_7),
    .out_8(n3_bit_comparator_1_out_8));
  _3_bit_comparator u_3_bit_comparator_2 (
    .input1(input1[14:12]), .lt_input(n3_bit_comparator_1_out_6), .eq_input(n3_bit_comparator_1_out_7),
    .gt_input(n3_bit_comparator_1_out_8), .input2(input2[14:12]), .out_6(n3_bit_comparator_2_out_6),
    .out_7(n3_bit_comparator_2_out_7), .out_8(n3_bit_comparator_2_out_8));
  _3_bit_comparator u_3_bit_comparator_3 (
    .input1(input1[11:9]), .lt_input(n3_bit_comparator_2_out_6), .eq_input(n3_bit_comparator_2_out_7),
    .gt_input(n3_bit_comparator_2_out_8), .input2(input2[11:9]), .out_6(n3_bit_comparator_3_out_6),
    .out_7(n3_bit_comparator_3_out_7), .out_8(n3_bit_comparator_3_out_8));
  _3_bit_comparator u_3_bit_comparator_4 (
    .input1(input1[8:6]), .lt_input(n3_bit_comparator_3_out_6), .eq_input(n3_bit_comparator_3_out_7),
    .gt_input(n3_bit_comparator_3_out_8), .input2(input2[8:6]), .out_6(n3_bit_comparator_4_out_6),
    .out_7(n3_bit_comparator_4_out_7), .out_8(n3_bit_comparator_4_out_8));
  _3_bit_comparator u_3_bit_comparator_5 (
    .input1(input1[5:3]), .lt_input(n3_bit_comparator_4_out_6), .eq_input(n3_bit_comparator_4_out_7),
    .gt_input(n3_bit_comparator_4_out_8), .input2(input2[5:3]), .out_6(n3_bit_comparator_5_out_6),
    .out_7(n3_bit_comparator_5_out_7), .out_8(n3_bit_comparator_5_out_8));
  _3_bit_comparator u_3_bit_comparator_6 (
    .input1(input1[2:0]), .lt_input(n3_bit_comparator_5_out_6), .eq_input(n3_bit_comparator_5_out_7),
    .gt_input(n3_bit_comparator_5_out_8), .input2(input2[2:0]), .out_6(\output [0]), .out_7(\output [1]),
    .out_8(\output [2]));
endmodule

// Control Unit
module ControlUnit (
  input  [17:0] Instruction,
  input  clockEnabled,
  output [13:0] jump_addr,
  output [3:0] src1_op2,
  output [3:0] src2,
  output [5:0] imm,
  output [3:0] dest_op1,
  output [9:0] addr,
  output [2:0] nzp,
  output [17:0] imm_extend,
  output Immediate,
  output [1:0] ALU_2,
  output aluControlSignal,
  output regWrite,
  output dataMemRead,
  output isStore,
  output dataMemWrite,
  output pcReadSignal,
  output isBranch,
  output PCselect,
  output isclock,
  output [2:0] fsControl
);

  wire ADD, ADDI, ALUcontrol, AND, ANDI, BEQ, BGE, BGT, BLE, BLT, BranchControl, JUMP, LD, OR, or_1_out,
       or_2_out, or_3_out, or_4_out, ORI, ST, XOR, XORI;
  wire [1:0] priority_encoder_1_out;
  wire [6:0] register_1_q;

  or or_1 (or_1_out, ADD, ADDI);
  or or_2 (or_2_out, AND, ANDI);
  or or_3 (or_3_out, OR, ORI);
  or or_4 (or_4_out, XOR, XORI);
  or or_5 (BranchControl, BGT, BEQ, BGE, BLT, BLE);
  Multiplexer #(.width(3), .enable("false")) multiplexer_1 (
    .in0(3'b000), .in1(Instruction[16:14]), .out(nzp), .sel(BranchControl));
  or or_6 (ALUcontrol, or_1_out, or_2_out, or_3_out, or_4_out);
  // Probe on ALUcontrol
  Priority_Encoder #(.select(2)) priority_encoder_1 (
    .in0(or_1_out), .in1(or_2_out), .in2(or_3_out), .in3(or_4_out), .out(priority_encoder_1_out));  // open: gs, en_out, en_in
  Register #(.width(7)) register_1 (
    .D({aluControlSignal, regWrite, dataMemRead, isStore, dataMemWrite, PCselect, isBranch}), .en(1'b1),
    .Q(register_1_q), .clk(clockEnabled));  // open: clr
  // Probe on Instruction[17:14]
  or or_7 (Immediate, ANDI, ADDI, ORI, XOR);
  FiniteStateMachine finitestatemachine_1 (
    .pc(register_1_q[6]), .clock(register_1_q[5]), .ALUcontrol(register_1_q[4]),
    .dataMemRead(register_1_q[3]), .regWrite(register_1_q[2]), .isST(register_1_q[1]),
    .MemWrite(register_1_q[0]), .fs_0(fsControl[2]), .fs_1(fsControl[1]), .fs_2(fsControl[0]),
    .isALU(aluControlSignal), .isRegWrite(regWrite), .isMemoryRead(dataMemRead), .isST_2(isStore),
    .isWriteMem(dataMemWrite), .PcSelect(PCselect), .isPCread(isBranch), .isClock(isclock));
  Priority_Encoder priority_encoder_2 (
    .in0(ALUcontrol), .in1(LD), .in2(ST), .in3(JUMP), .in4(BranchControl), .out(fsControl));  // open: in5, in6, in7, en_in
  Decoder #(.select(4)) decoder_1 (
    .out0(AND), .out1(ANDI), .out2(ADD), .out3(ADDI), .out4(OR), .out5(ORI), .out6(XOR), .out7(XORI),
    .out8(LD), .out9(BGT), .out10(BEQ), .out11(BGE), .out12(BLT), .out13(ST), .out14(BLE), .out15(JUMP),
    .sel(Instruction[17:14]));  // open: en
  Multiplexer #(.width(2), .enable("false")) multiplexer_2 (
    .in0(2'b00), .in1(priority_encoder_1_out), .out(ALU_2), .sel(ALUcontrol));
  // Probe on Instruction[9:0]
  _6_18_bit_extender__Imm u_6_18_bit_extender_imm_1 (
    .Immediate_value(Instruction[5:0]), .Extended_immediate_value(imm_extend));

  assign addr = Instruction[9:0];
  assign dest_op1 = Instruction[13:10];
  assign imm = Instruction[5:0];
  assign jump_addr = Instruction[13:0];
  assign pcReadSignal = isBranch;
  assign src1_op2 = Instruction[9:6];
  assign src2 = Instruction[3:0];

  // Other names for the same wires on the sheet: immValue[5:0] = Instruction[5:0]; DEST[3:0] = Instruction[13:10];
  //   OP1[3:0] = Instruction[13:10]

  // Notes on the sheet:
  //   DEST ADDRESS
  //   Sequence Depend on ALU operation
  //   SRC1 OP1 IMM ADDRESS
  //   SRC2 OP2 IMM ADDRESS
  //   ST LD ADDRESS
  //   JUMP ADDRESS
endmodule

module Processor (
  input  clear,
  input  clear_2,
  input  enable
);

  wire ALU, Clock, clock_t, ClockEnabled, DMR, DMW, IMM, isBR, isStore, PCR, PCS, RW;
  wire [1:0] ALU_2;
  wire [2:0] comparator_1_output, FSC, NZP;
  wire [3:0] demultiplexer_1_out0, demultiplexer_1_out1, demultiplexer_2_out1, DEST, dest_op1,
       multiplexer_2_out, SRC1, src1_op2, SRC2, src2_t;
  wire [5:0] imm_addr;
  wire [9:0] ADDR;
  wire [13:0] jump_addr;
  wire [17:0] alu_1_aluresult, imm_extend, multiplexer_4_out, multiplexer_5_out, multiplexer_6_out,
       n14_18_bit_extender_jump_addr_1_extended_jump_addr, pc_1_pc_address, ram_1_data,
       register_file_1_reg1databinary, register_file_1_reg2databinary, rom_1_data,
       unsigned_extender_6_18_1_extended_branch_addr;

  Demultiplexer #(.width(4), .enable("false")) demultiplexer_1 (
    .out0(demultiplexer_1_out0), .out1(demultiplexer_1_out1), .in(src1_op2), .sel(isBR));
  Clock clock_1 (.out(Clock));
  Demultiplexer #(.width(4), .enable("false")) demultiplexer_2 (
    .out0(DEST), .out1(demultiplexer_2_out1), .in(dest_op1), .sel(isBR));
  ROM #(.addrWidth(18), .dataWidth(18)) rom_1 (.addr(pc_1_pc_address), .data(rom_1_data), .sel(1'b1));
  Multiplexer #(.width(4), .enable("false")) multiplexer_1 (
    .in0(src2_t), .in1(demultiplexer_1_out1), .out(SRC2), .sel(isBR));
  Multiplexer #(.width(4), .enable("false")) multiplexer_2 (
    .in0(demultiplexer_1_out0), .in1(demultiplexer_2_out1), .out(multiplexer_2_out), .sel(isBR));
  ControlUnit controlunit_1 (
    .jump_addr(jump_addr), .dest_op1(dest_op1), .Instruction(rom_1_data), .nzp(NZP),
    .clockEnabled(ClockEnabled), .Immediate(IMM), .addr(ADDR), .src1_op2(src1_op2), .src2(src2_t),
    .imm(imm_addr), .imm_extend(imm_extend), .ALU_2(ALU_2), .aluControlSignal(ALU), .regWrite(RW),
    .dataMemRead(DMR), .isStore(isStore), .dataMemWrite(DMW), .pcReadSignal(PCR), .isBranch(isBR),
    .PCselect(PCS), .isclock(clock_t), .fsControl(FSC));
  Multiplexer #(.width(4), .enable("false")) multiplexer_3 (
    .in0(multiplexer_2_out), .in1(dest_op1), .out(SRC1), .sel(isStore));
  _14_18_bit_extender__jump_addr u_14_18_bit_extender_jump_addr_1 (
    .Jump_addr(jump_addr), .extended_jump_addr(n14_18_bit_extender_jump_addr_1_extended_jump_addr));
  Unsigned_extender__6_18 unsigned_extender_6_18_1 (
    .branch_addr(imm_addr), .extended_branch_addr(unsigned_extender_6_18_1_extended_branch_addr));
  PC pc_1 (
    .Addr(multiplexer_4_out), .nzp(NZP), .cmp(comparator_1_output), .enable(enable), .clock(Clock),
    .clear(clear_2), .isJump(PCS), .PC_Address(pc_1_pc_address));
  Comparator comparator_1 (
    .input1(register_file_1_reg1databinary), .lt_input(NZP[2]), .eq_input(NZP[1]), .gt_input(NZP[0]),
    .input2(register_file_1_reg2databinary), .\output (comparator_1_output));
  Multiplexer #(.width(18), .enable("false")) multiplexer_4 (
    .in0(n14_18_bit_extender_jump_addr_1_extended_jump_addr),
    .in1(unsigned_extender_6_18_1_extended_branch_addr), .out(multiplexer_4_out), .sel(isBR));
  RAM #(.addrWidth(10), .dataWidth(18), .bus("separate")) ram_1 (
    .addr(ADDR), .din(register_file_1_reg1databinary), .data(ram_1_data), .str(DMW), .clk(Clock), .ld(DMR));  // open: sel, clr
  Register_File register_file_1 (
    .inputData(multiplexer_6_out), .ReadReg1Address(SRC1), .ReadReg2Address(SRC2), .destReg(DEST),
    .registerWrite(RW), .Clock(Clock), .Clear(clear), .Reg1DataBinary(register_file_1_reg1databinary),
    .Reg2DataBinary(register_file_1_reg2databinary));
  Multiplexer #(.width(18), .enable("false")) multiplexer_5 (
    .in0(register_file_1_reg1databinary), .in1(imm_extend), .out(multiplexer_5_out), .sel(IMM));
  ALU alu_1 (
    .ALUcontrol(ALU_2), .src1(register_file_1_reg2databinary), .src2(multiplexer_5_out),
    .ALUresult(alu_1_aluresult));
  Multiplexer #(.width(18), .enable("false")) multiplexer_6 (
    .in0(ram_1_data), .in1(alu_1_aluresult), .out(multiplexer_6_out), .sel(ALU));

  // Notes on the sheet:
  //   Inst Mem
  //   contents of rom_1 (hex, n*v repeats v):
  //   ea82 fb81 ff40 f780 bb4f 2a683 ffd0 37c00 e641 3fffb
  //   Data Mem
endmodule

// FiniteState
module FiniteStateMachine (
  input  pc,
  input  clock,
  input  ALUcontrol,
  input  dataMemRead,
  input  regWrite,
  input  isST,
  input  MemWrite,
  input  fs_0,
  input  fs_1,
  input  fs_2,
  output isALU,
  output isRegWrite,
  output isMemoryRead,
  output isST_2,
  output isWriteMem,
  output PcSelect,
  output isPCread,
  output isClock
);

  wire and_1_out, and_2_out, and_3_out, is_Operation, not_1_out, not_2_out, not_3_out, not_4_out, not_5_out,
       not_6_out, not_7_out, not_8_out, not_9_out, not_10_out, not_11_out, not_12_out, not_13_out,
       not_14_out, pc_clock_activate;

  not not_1 (not_1_out, pc);
  not not_2 (not_2_out, clock);
  not not_3 (not_3_out, clock);
  not not_4 (not_4_out, pc);
  and and_1 (and_1_out, not_1_out, not_2_out);
  and and_2 (and_2_out, pc, not_3_out);
  and and_3 (and_3_out, not_4_out, clock);
  or or_1 (pc_clock_activate, and_1_out, and_2_out, and_3_out);
  // Probe on pc_clock_activate
  nor nor_1 (is_Operation, ALUcontrol, dataMemRead, regWrite, isST, MemWrite);
  not not_5 (not_5_out, fs_0);
  not not_6 (not_6_out, fs_1);
  not not_7 (not_7_out, fs_2);
  not not_8 (not_8_out, fs_0);
  not not_9 (not_9_out, fs_1);
  not not_10 (not_10_out, fs_0);
  not not_11 (not_11_out, fs_2);
  not not_12 (not_12_out, fs_0);
  not not_13 (not_13_out, fs_1);
  not not_14 (not_14_out, fs_2);
  and and_4 (isALU, pc_clock_activate, is_Operation, not_5_out, not_6_out, not_7_out);
  and and_5 (isMemoryRead, pc_clock_activate, is_Operation, not_8_out, not_9_out, fs_2);
  and and_6 (isST_2, pc_clock_activate, is_Operation, not_10_out, fs_1, not_11_out);
  and and_7 (PcSelect, pc_clock_activate, is_Operation, not_12_out, fs_1, fs_2);
  and and_8 (isPCread, pc_clock_activate, is_Operation, fs_0, not_13_out, not_14_out);
  or or_2 (isRegWrite, isALU, isMemoryRead);

  assign isClock = clock;
  assign isWriteMem = isST_2;

  // Notes on the sheet:
  //   clock counter enabled gerekli mi 
endmodule

// 6-18
module _6_18_bit_extender__Imm (
  input  [5:0] Immediate_value,
  output [17:0] Extended_immediate_value
);


  assign Extended_immediate_value = {{13{Immediate_value[5]}}, Immediate_value[4:0]};
endmodule

// 14-18
module _14_18_bit_extender__jump_addr (
  input  [13:0] Jump_addr,
  output [17:0] extended_jump_addr
);


  assign extended_jump_addr = {{5{Jump_addr[13]}}, Jump_addr[12:0]};
endmodule

// 6-18
module Unsigned_extender__6_18 (
  input  [5:0] branch_addr,
  output [17:0] extended_branch_addr
);


  assign extended_branch_addr = {{12{1'b0}}, branch_addr};
endmodule
